// Logisim project memoryGame.circ as structural Verilog: 2 circuits, main circuit main
module main (
);

  wire and_1_out, and_2_out, and_3_out, and_4_out, and_5_out, and_6_out, and_7_out, and_8_out, and_9_out,
       and_10_out, and_11_out, and_12_out, and_13_out, and_14_out, and_15_out, and_16_out, and_17_out,
       and_18_out, and_19_out, and_20_out, and_21_out, and_22_out, and_23_out, and_24_out, and_25_out,
       and_26_out, and_27_out, and_28_out, and_29_out, and_30_out, and_31_out, and_32_out, and_33_out,
       and_34_out, and_35_out, and_36_out, and_37_out, and_38_out, and_39_out, and_40_out, and_41_out,
       and_42_out, and_43_out, and_44_out, and_45_out, and_46_out, and_47_out, and_48_out, and_49_out,
       and_50_out, and_51_out, and_52_out, and_53_out, and_54_out, and_55_out, and_56_out, and_57_out,
       and_58_out, and_59_out, and_60_out, and_61_out, and_62_out, and_63_out, and_64_out, and_65_out,
       and_66_out, and_67_out, and_68_out, and_69_out, and_70_out, and_71_out, and_72_out, and_73_out,
       and_74_out, and_79_out, and_80_out, and_81_out, and_82_out, and_83_out, and_84_out, and_85_out,
       and_86_out, and_87_out, and_88_out, and_89_out, and_90_out, and_91_out, and_92_out, and_93_out,
       and_94_out, and_95_out, and_96_out, and_97_out, and_98_out, and_99_out, and_100_out, and_101_out,
       and_102_out, and_104_out, and_105_out, COLUNA, comparator_1_eq, comparator_2_eq, comparator_3_eq,
       comparator_4_eq, comparator_5_eq, comparator_6_eq, comparator_7_eq, comparator_8_eq, comparator_9_eq,
       comparator_10_eq, comparator_11_eq, comparator_12_eq, comparator_13_eq, comparator_14_eq,
       comparator_15_eq, comparator_16_eq, comparator_17_eq, comparator_18_eq, comparator_19_eq,
       comparator_20_eq, comparator_21_eq, comparator_22_eq, comparator_23_eq, comparator_24_eq,
       comparator_25_eq, comparator_26_eq, comparator_26_gt, comparator_26_lt, comparator_27_eq,
       comparator_28_eq, comparator_29_eq, comparator_30_eq, comparator_31_eq, comparator_32_eq,
       comparator_33_eq, comparator_34_eq, comparator_35_eq, CONFIRMA, CONFIRMAR, correct, correct_00,
       correct_01, correct_02, correct_03, correct_10, correct_11, correct_12, correct_13, correct_20,
       correct_21, correct_22, correct_23, correct_30, correct_31, correct_32, correct_33, counter_1_q,
       counter_2_q, counter_3_q, counter_4_q, counter_5_q, counter_6_q, counter_7_q, counter_8_q,
       counter_9_q, counter_11_q, counter_12_q, counter_13_q, counter_14_q, counter_15_q, counter_16_q,
       counter_17_q, FIM, L00, L01, L02, L03, L10, L11, L12, L13, L20, L21, L22, L23, L30, L31, L32, L33,
       LINHA, multiplexer_19_out, or_17_out, or_18_out, or_19_out, or_20_out, or_21_out, or_22_out,
       or_23_out, or_24_out, or_25_out, or_26_out, or_27_out, or_28_out, or_29_out, or_30_out, or_31_out,
       or_32_out, or_33_out, P1, P2, state0, state1, state2, state3, v00, v01, v02, v03, v10, v11, v12, v13,
       v20, v21, v22, v23, v30, v31, v32, v33, winP0, winP1, winP2;
  wire [1:0] COL, COL1, COL2, counter_10_q, LIN, LIN1, LIN2;
  wire [3:0] _00, _01, _02, _03, _10, _11, _12, _13, _20, _21, _22, _23, _30, _31, _32, _33, adder_1_out,
       PONTOS_P1, PONTOS_P2, valueXY1, valueXY2;

  Multiplexer #(.width(4), .enable("false")) multiplexer_1 (.in1(4'b0011), .out(_00), .sel(v00));  // open: in0
  Multiplexer #(.width(4), .enable("false")) multiplexer_2 (.in1(4'b0000), .out(_10), .sel(v10));  // open: in0
  Multiplexer #(.width(4), .enable("false")) multiplexer_3 (.in1(4'b0001), .out(_20), .sel(v20));  // open: in0
  Multiplexer #(.width(4), .enable("false")) multiplexer_4 (.in1(4'b0011), .out(_30), .sel(v30));  // open: in0
  Multiplexer #(.width(4), .enable("false")) multiplexer_5 (.in1(4'b0010), .out(_01), .sel(v01));  // open: in0
  Multiplexer #(.width(4), .enable("false")) multiplexer_6 (.in1(4'b1111), .out(_11), .sel(v11));  // open: in0
  Multiplexer #(.width(4), .enable("false")) multiplexer_7 (.in1(4'b1010), .out(_21), .sel(v21));  // open: in0
  Multiplexer #(.width(4), .enable("false")) multiplexer_8 (.in1(4'b1110), .out(_31), .sel(v31));  // open: in0
  and and_1 (and_1_out, ~LIN1[0], ~LIN1[1]);  // AND_Gate
  and and_2 (and_2_out, ~COL1[0], ~COL1[1]);  // AND_Gate
  and and_3 (and_3_out, ~LIN2[0], ~LIN2[1]);  // AND_Gate
  and and_4 (and_4_out, ~COL2[0], ~COL2[1]);  // AND_Gate
  and and_5 (and_5_out, LIN1[0], ~LIN1[1]);  // AND_Gate
  and and_6 (and_6_out, ~COL1[0], ~COL1[1]);  // AND_Gate
  and and_7 (and_7_out, LIN2[0], ~LIN2[1]);  // AND_Gate
  and and_8 (and_8_out, ~COL2[0], ~COL2[1]);  // AND_Gate
  and and_9 (and_9_out, ~LIN1[0], LIN1[1]);  // AND_Gate
  and and_10 (and_10_out, ~COL1[0], ~COL1[1]);  // AND_Gate
  and and_11 (and_11_out, ~LIN2[0], LIN2[1]);  // AND_Gate
  and and_12 (and_12_out, ~COL2[0], ~COL2[1]);  // AND_Gate
  and and_13 (and_13_out, LIN1[0], LIN1[1]);
  and and_14 (and_14_out, ~COL1[0], ~COL1[1]);  // AND_Gate
  and and_15 (and_15_out, LIN2[0], LIN2[1]);
  and and_16 (and_16_out, ~COL2[0], ~COL2[1]);  // AND_Gate
  Multiplexer #(.width(4), .enable("false")) multiplexer_9 (.in1(4'b1111), .out(_02), .sel(v02));  // open: in0
  Multiplexer #(.width(4), .enable("false")) multiplexer_10 (.in1(4'b0000), .out(_12), .sel(v12));  // open: in0
  Multiplexer #(.width(4), .enable("false")) multiplexer_11 (.in1(4'b0010), .out(_22), .sel(v22));  // open: in0
  Multiplexer #(.width(4), .enable("false")) multiplexer_12 (.in1(4'b1010), .out(_32), .sel(v32));  // open: in0
  and and_17 (and_17_out, ~state0, and_1_out, and_2_out);  // AND_Gate
  or or_1 (v00, and_17_out, and_18_out, counter_1_q);
  Counter #(.width(1), .max('h1), .ongoal("stay")) counter_1 (
    .Q(counter_1_q), .clk(correct_00));  // open: load, D, count, carry, clr
  and and_18 (and_18_out, state2, and_3_out, and_4_out);
  and and_19 (and_19_out, ~state0, and_5_out, and_6_out);  // AND_Gate
  and and_20 (and_20_out, state2, and_7_out, and_8_out);
  and and_21 (and_21_out, ~state0, and_9_out, and_10_out);  // AND_Gate
  and and_22 (and_22_out, state2, and_11_out, and_12_out);
  and and_23 (and_23_out, ~state0, and_13_out, and_14_out);  // AND_Gate
  and and_24 (and_24_out, state2, and_15_out, and_16_out);
  or or_2 (v10, and_19_out, and_20_out, counter_2_q);
  Counter #(.width(1), .max('h1), .ongoal("stay")) counter_2 (
    .Q(counter_2_q), .clk(correct_10));  // open: load, D, count, carry, clr
  or or_3 (v20, and_21_out, and_22_out, counter_3_q);
  Counter #(.width(1), .max('h1), .ongoal("stay")) counter_3 (
    .Q(counter_3_q), .clk(correct_20));  // open: load, D, count, carry, clr
  or or_4 (v30, and_23_out, and_24_out, counter_4_q);
  Counter #(.width(1), .max('h1), .ongoal("stay")) counter_4 (
    .Q(counter_4_q), .clk(correct_30));  // open: load, D, count, carry, clr
  Button button_1 (.out(CONFIRMAR));
  Button button_2 (.out(LINHA));
  Button button_3 (.out(COLUNA));
  LED led_1 (.in(winP1));
  LED led_2 (.in(winP0));
  LED led_3 (.in(winP2));
  Multiplexer #(.width(4), .enable("false")) multiplexer_13 (.in1(4'b0101), .out(_03), .sel(v03));  // open: in0
  Multiplexer #(.width(4), .enable("false")) multiplexer_14 (.in1(4'b0001), .out(_13), .sel(v13));  // open: in0
  Multiplexer #(.width(4), .enable("false")) multiplexer_15 (.in1(4'b1110), .out(_23), .sel(v23));  // open: in0
  Multiplexer #(.width(4), .enable("false")) multiplexer_16 (.in1(4'b0101), .out(_33), .sel(v33));  // open: in0
  and and_25 (and_25_out, ~LIN1[0], ~LIN1[1]);  // AND_Gate
  and and_26 (and_26_out, COL1[0], ~COL1[1]);  // AND_Gate
  and and_27 (and_27_out, ~LIN2[0], ~LIN2[1]);  // AND_Gate
  and and_28 (and_28_out, COL2[0], ~COL2[1]);  // AND_Gate
  and and_29 (and_29_out, LIN1[0], ~LIN1[1]);  // AND_Gate
  and and_30 (and_30_out, COL1[0], ~COL1[1]);  // AND_Gate
  and and_31 (and_31_out, LIN2[0], ~LIN2[1]);  // AND_Gate
  and and_32 (and_32_out, COL2[0], ~COL2[1]);  // AND_Gate
  LED led_4 (.in(L00));
  Hex_Digit_Display hex_digit_display_1 (.value(_00));  // open: dp
  LED led_5 (.in(L10));
  Hex_Digit_Display hex_digit_display_2 (.value(_10));  // open: dp
  LED led_6 (.in(L20));
  Hex_Digit_Display hex_digit_display_3 (.value(_20));  // open: dp
  LED led_7 (.in(L30));
  Hex_Digit_Display hex_digit_display_4 (.value(_30));  // open: dp
  and and_33 (and_33_out, ~state0, and_25_out, and_26_out);  // AND_Gate
  Counter #(.width(1), .max('h1), .ongoal("stay")) counter_5 (
    .Q(counter_5_q), .clk(correct_01));  // open: load, D, count, carry, clr
  and and_34 (and_34_out, state2, and_27_out, and_28_out);
  and and_35 (and_35_out, ~state0, and_29_out, and_30_out);  // AND_Gate
  and and_36 (and_36_out, state2, and_31_out, and_32_out);
  and and_37 (and_37_out, ~LIN1[0], LIN1[1]);  // AND_Gate
  and and_38 (and_38_out, ~state0, and_37_out, and_39_out);  // AND_Gate
  and and_39 (and_39_out, COL1[0], ~COL1[1]);  // AND_Gate
  and and_40 (and_40_out, ~LIN2[0], LIN2[1]);  // AND_Gate
  and and_41 (and_41_out, state2, and_40_out, and_42_out);
  and and_42 (and_42_out, COL2[0], ~COL2[1]);  // AND_Gate
  and and_43 (and_43_out, LIN1[0], LIN1[1]);
  and and_44 (and_44_out, COL1[0], ~COL1[1]);  // AND_Gate
  and and_45 (and_45_out, LIN2[0], LIN2[1]);
  and and_46 (and_46_out, COL2[0], ~COL2[1]);  // AND_Gate
  LED led_8 (.in(L01));
  Hex_Digit_Display hex_digit_display_5 (.value(_01));  // open: dp
  LED led_9 (.in(L11));
  Hex_Digit_Display hex_digit_display_6 (.value(_11));  // open: dp
  LED led_10 (.in(L21));
  Hex_Digit_Display hex_digit_display_7 (.value(_21));  // open: dp
  LED led_11 (.in(L31));
  Hex_Digit_Display hex_digit_display_8 (.value(_31));  // open: dp
  and and_47 (and_47_out, CONFIRMA, state0);
  and and_48 (and_48_out, CONFIRMA, state1);
  or or_5 (v01, and_33_out, and_34_out, counter_5_q);
  or or_6 (v11, and_35_out, and_36_out, counter_6_q);
  Counter #(.width(1), .max('h1), .ongoal("stay")) counter_6 (
    .Q(counter_6_q), .clk(correct_11));  // open: load, D, count, carry, clr
  or or_7 (v21, and_38_out, and_41_out, counter_7_q);
  Counter #(.width(1), .max('h1), .ongoal("stay")) counter_7 (
    .Q(counter_7_q), .clk(correct_21));  // open: load, D, count, carry, clr
  and and_49 (and_49_out, ~state0, and_43_out, and_44_out);  // AND_Gate
  or or_8 (v31, and_49_out, and_50_out, counter_8_q);
  Counter #(.width(1), .max('h1), .ongoal("stay")) counter_8 (
    .Q(counter_8_q), .clk(correct_31));  // open: load, D, count, carry, clr
  and and_50 (and_50_out, state2, and_45_out, and_46_out);
  LED led_12 (.in(L02));
  Hex_Digit_Display hex_digit_display_9 (.value(_02));  // open: dp
  LED led_13 (.in(L12));
  Hex_Digit_Display hex_digit_display_10 (.value(_12));  // open: dp
  LED led_14 (.in(L22));
  Hex_Digit_Display hex_digit_display_11 (.value(_22));  // open: dp
  LED led_15 (.in(L32));
  Hex_Digit_Display hex_digit_display_12 (.value(_32));  // open: dp
  Register #(.width(2)) register_1 (.D(COL), .Q(COL1), .clk(and_47_out));  // open: en, clr
  Register #(.width(2)) register_2 (.D(COL), .Q(COL2), .clk(and_48_out));  // open: en, clr
  LED led_16 (.in(L03));
  Hex_Digit_Display hex_digit_display_13 (.value(_03));  // open: dp
  LED led_17 (.in(L13));
  Hex_Digit_Display hex_digit_display_14 (.value(_13));  // open: dp
  LED led_18 (.in(L23));
  Hex_Digit_Display hex_digit_display_15 (.value(_23));  // open: dp
  LED led_19 (.in(L33));
  Hex_Digit_Display hex_digit_display_16 (.value(_33));  // open: dp
  Register #(.width(2)) register_3 (.D(LIN), .Q(LIN1), .clk(and_47_out));  // open: en, clr
  Register #(.width(2)) register_4 (.D(LIN), .Q(LIN2), .clk(and_48_out));  // open: en, clr
  and and_51 (and_51_out, ~LIN1[0], ~LIN1[1]);  // AND_Gate
  and and_52 (and_52_out, ~COL1[0], COL1[1]);  // AND_Gate
  and and_53 (and_53_out, ~LIN2[0], ~LIN2[1]);  // AND_Gate
  and and_54 (and_54_out, ~COL2[0], COL2[1]);  // AND_Gate
  and and_55 (and_55_out, LIN1[0], ~LIN1[1]);  // AND_Gate
  and and_56 (and_56_out, ~COL1[0], COL1[1]);  // AND_Gate
  and and_57 (and_57_out, LIN2[0], ~LIN2[1]);  // AND_Gate
  and and_58 (and_58_out, ~COL2[0], COL2[1]);  // AND_Gate
  and and_59 (and_59_out, ~LIN1[0], LIN1[1]);  // AND_Gate
  and and_60 (and_60_out, ~COL1[0], COL1[1]);  // AND_Gate
  and and_61 (and_61_out, ~LIN2[0], LIN2[1]);  // AND_Gate
  and and_62 (and_62_out, ~COL2[0], COL2[1]);  // AND_Gate
  and and_63 (and_63_out, LIN1[0], LIN1[1]);
  and and_64 (and_64_out, ~COL1[0], COL1[1]);  // AND_Gate
  and and_65 (and_65_out, LIN2[0], LIN2[1]);
  and and_66 (and_66_out, ~COL2[0], COL2[1]);  // AND_Gate
  and and_67 (and_67_out, ~state0, and_51_out, and_52_out);  // AND_Gate
  or or_9 (v02, and_67_out, and_68_out, counter_9_q);
  Counter #(.width(1), .max('h1), .ongoal("stay")) counter_9 (
    .Q(counter_9_q), .clk(correct_02));  // open: load, D, count, carry, clr
  and and_68 (and_68_out, state2, and_53_out, and_54_out);
  and and_69 (and_69_out, ~state0, and_55_out, and_56_out);  // AND_Gate
  and and_70 (and_70_out, state2, and_57_out, and_58_out);
  and and_71 (and_71_out, ~state0, and_59_out, and_60_out);  // AND_Gate
  and and_72 (and_72_out, state2, and_61_out, and_62_out);
  and and_73 (and_73_out, ~state0, and_63_out, and_64_out);  // AND_Gate
  and and_74 (and_74_out, state2, and_65_out, and_66_out);
  LED led_20 (.in(P1));
  Hex_Digit_Display hex_digit_display_17 (.value(PONTOS_P1));  // open: dp
  LED led_21 (.in(P2));
  Hex_Digit_Display hex_digit_display_18 (.value(PONTOS_P2));  // open: dp
  Counter #(.width(2), .max('h3)) counter_10 (
    .Q(counter_10_q), .clk(CONFIRMA), .clr(state3));  // open: load, D, count, carry
  or or_10 (v12, and_69_out, and_70_out, counter_11_q);
  Counter #(.width(1), .max('h1), .ongoal("stay")) counter_11 (
    .Q(counter_11_q), .clk(correct_12));  // open: load, D, count, carry, clr
  or or_11 (v22, and_71_out, and_72_out, counter_12_q);
  Counter #(.width(1), .max('h1), .ongoal("stay")) counter_12 (
    .Q(counter_12_q), .clk(correct_22));  // open: load, D, count, carry, clr
  or or_12 (v32, and_73_out, and_74_out, counter_13_q);
  Counter #(.width(1), .max('h1), .ongoal("stay")) counter_13 (
    .Q(counter_13_q), .clk(correct_32));  // open: load, D, count, carry, clr
  and and_75 (state0, ~counter_10_q[0], ~counter_10_q[1]);  // AND_Gate
  and and_76 (state1, ~counter_10_q[1], counter_10_q[0]);  // AND_Gate
  and and_77 (state2, counter_10_q[1], ~counter_10_q[0]);  // AND_Gate
  and and_78 (state3, counter_10_q[1], counter_10_q[0]);
  and and_79 (and_79_out, ~LIN1[0], ~LIN1[1]);  // AND_Gate
  and and_80 (and_80_out, COL1[0], COL1[1]);
  and and_81 (and_81_out, ~LIN2[0], ~LIN2[1]);  // AND_Gate
  and and_82 (and_82_out, COL2[0], COL2[1]);
  and and_83 (and_83_out, LIN1[0], ~LIN1[1]);  // AND_Gate
  and and_84 (and_84_out, COL1[0], COL1[1]);
  and and_85 (and_85_out, LIN2[0], ~LIN2[1]);  // AND_Gate
  and and_86 (and_86_out, COL2[0], COL2[1]);
  and and_87 (and_87_out, ~LIN1[0], LIN1[1]);  // AND_Gate
  and and_88 (and_88_out, COL1[0], COL1[1]);
  and and_89 (and_89_out, ~LIN2[0], LIN2[1]);  // AND_Gate
  and and_90 (and_90_out, COL2[0], COL2[1]);
  and and_91 (and_91_out, ~state0, and_79_out, and_80_out);  // AND_Gate
  and and_92 (and_92_out, state2, and_81_out, and_82_out);
  and and_93 (and_93_out, ~state0, and_83_out, and_84_out);  // AND_Gate
  and and_94 (and_94_out, state2, and_85_out, and_86_out);
  and and_95 (and_95_out, ~state0, and_87_out, and_88_out);  // AND_Gate
  and and_96 (and_96_out, state2, and_89_out, and_90_out);
  and and_97 (and_97_out, LIN1[0], LIN1[1]);
  and and_98 (and_98_out, ~state0, and_97_out, and_99_out);  // AND_Gate
  and and_99 (and_99_out, COL1[0], COL1[1]);
  and and_100 (and_100_out, LIN2[0], LIN2[1]);
  and and_101 (and_101_out, state2, and_100_out, and_102_out);
  and and_102 (and_102_out, COL2[0], COL2[1]);
  or or_13 (v03, and_91_out, and_92_out, counter_14_q);
  Counter #(.width(1), .max('h1), .ongoal("stay")) counter_14 (
    .Q(counter_14_q), .clk(correct_03));  // open: load, D, count, carry, clr
  or or_14 (v13, and_93_out, and_94_out, counter_15_q);
  Counter #(.width(1), .max('h1), .ongoal("stay")) counter_15 (
    .Q(counter_15_q), .clk(correct_13));  // open: load, D, count, carry, clr
  or or_15 (v23, and_95_out, and_96_out, counter_16_q);
  Counter #(.width(1), .max('h1), .ongoal("stay")) counter_16 (
    .Q(counter_16_q), .clk(correct_23));  // open: load, D, count, carry, clr
  or or_16 (v33, and_98_out, and_101_out, counter_17_q);
  Counter #(.width(1), .max('h1), .ongoal("stay")) counter_17 (
    .Q(counter_17_q), .clk(correct_33));  // open: load, D, count, carry, clr
  Counter #(.width(2), .max('h3)) counter_18 (.Q(COL), .clk(COLUNA));  // open: load, D, count, carry, clr
  Counter #(.width(2), .max('h3)) counter_19 (.Q(LIN), .clk(LINHA));  // open: load, D, count, carry, clr
  Multiplexer #(.select(4), .width(4), .enable("false")) multiplexer_17 (
    .in0(_00), .in1(_01), .in2(_02), .in3(_03), .in4(_10), .in5(_11), .in6(_12), .in7(_13), .in8(_20),
    .in9(_21), .in10(_22), .in11(_23), .in12(_30), .in13(_31), .in14(_32), .in15(_33), .out(valueXY1),
    .sel({LIN1, COL1}));
  Demultiplexer #(.select(4), .enable("false")) demultiplexer_1 (
    .out0(L00), .out1(L01), .out2(L02), .out3(L03), .out4(L10), .out5(L11), .out6(L12), .out7(L13),
    .out8(L20), .out9(L21), .out10(L22), .out11(L23), .out12(L30), .out13(L31), .out14(L32), .out15(L33),
    .in(1'b1), .sel({LIN, COL}));
  Comparator #(.width(4)) comparator_1 (.a(valueXY1), .b(valueXY2), .eq(comparator_1_eq));  // open: gt, lt
  and and_103 (correct, comparator_1_eq, state3);
  Multiplexer #(.select(4), .width(4), .enable("false")) multiplexer_18 (
    .in0(_00), .in1(_01), .in2(_02), .in3(_03), .in4(_10), .in5(_11), .in6(_12), .in7(_13), .in8(_20),
    .in9(_21), .in10(_22), .in11(_23), .in12(_30), .in13(_31), .in14(_32), .in15(_33), .out(valueXY2),
    .sel({LIN2, COL2}));
  Counter #(.width(4), .max('h8), .ongoal("stay")) counter_20 (
    .Q(PONTOS_P1), .clk(and_104_out));  // open: load, D, count, carry, clr
  and and_104 (and_104_out, ~P2, correct);  // AND_Gate
  Counter #(.width(1), .max('h1), .trigger("falling")) counter_21 (
    .Q(P2), .clk(state3));  // open: load, D, count, carry, clr
  and and_105 (and_105_out, P2, correct);
  Multiplexer #(.select(4), .enable("false")) multiplexer_19 (
    .in0(v00), .in1(v01), .in2(v02), .in3(v03), .in4(v10), .in5(v11), .in6(v12), .in7(v13), .in8(v20),
    .in9(v21), .in10(v22), .in11(v23), .in12(v30), .in13(v31), .in14(v32), .in15(v33),
    .out(multiplexer_19_out), .sel({LIN, COL}));
  or or_17 (or_17_out, ~multiplexer_19_out, state2);  // OR_Gate
  Counter #(.width(4), .max('h8), .ongoal("stay")) counter_22 (
    .Q(PONTOS_P2), .clk(and_105_out));  // open: load, D, count, carry, clr
  and and_106 (CONFIRMA, CONFIRMAR, or_17_out);
  Comparator #(.width(4)) comparator_2 (.a({LIN1, COL1}), .b(4'b0000), .eq(comparator_2_eq));  // open: gt, lt
  or or_18 (or_18_out, comparator_2_eq, comparator_3_eq);
  Comparator #(.width(4)) comparator_3 (.a({LIN2, COL2}), .b(4'b0000), .eq(comparator_3_eq));  // open: gt, lt
  Comparator #(.width(4)) comparator_4 (.a({LIN1, COL1}), .b(4'b0100), .eq(comparator_4_eq));  // open: gt, lt
  or or_19 (or_19_out, comparator_4_eq, comparator_5_eq);
  Comparator #(.width(4)) comparator_5 (.a({LIN2, COL2}), .b(4'b0100), .eq(comparator_5_eq));  // open: gt, lt
  Comparator #(.width(4)) comparator_6 (.a({LIN1, COL1}), .b(4'b1000), .eq(comparator_6_eq));  // open: gt, lt
  or or_20 (or_20_out, comparator_6_eq, comparator_7_eq);
  Comparator #(.width(4)) comparator_7 (.a({LIN2, COL2}), .b(4'b1000), .eq(comparator_7_eq));  // open: gt, lt
  Comparator #(.width(4)) comparator_8 (.a({LIN1, COL1}), .b(4'b1100), .eq(comparator_8_eq));  // open: gt, lt
  or or_21 (or_21_out, comparator_8_eq, comparator_9_eq);
  Comparator #(.width(4)) comparator_9 (.a({LIN2, COL2}), .b(4'b1100), .eq(comparator_9_eq));  // open: gt, lt
  and and_107 (correct_00, or_18_out, correct);
  and and_108 (correct_10, or_19_out, correct);
  and and_109 (correct_20, or_20_out, correct);
  and and_110 (correct_30, or_21_out, correct);
  not not_1 (P1, P2);
  Comparator #(.width(4)) comparator_10 (.a({LIN1, COL1}), .b(4'b0001), .eq(comparator_10_eq));  // open: gt, lt
  Comparator #(.width(4)) comparator_11 (.a({LIN2, COL2}), .b(4'b0001), .eq(comparator_11_eq));  // open: gt, lt
  Comparator #(.width(4)) comparator_12 (.a({LIN1, COL1}), .b(4'b0101), .eq(comparator_12_eq));  // open: gt, lt
  Comparator #(.width(4)) comparator_13 (.a({LIN2, COL2}), .b(4'b0101), .eq(comparator_13_eq));  // open: gt, lt
  Comparator #(.width(4)) comparator_14 (.a({LIN1, COL1}), .b(4'b1001), .eq(comparator_14_eq));  // open: gt, lt
  Comparator #(.width(4)) comparator_15 (.a({LIN2, COL2}), .b(4'b1001), .eq(comparator_15_eq));  // open: gt, lt
  Comparator #(.width(4)) comparator_16 (.a({LIN1, COL1}), .b(4'b1101), .eq(comparator_16_eq));  // open: gt, lt
  Comparator #(.width(4)) comparator_17 (.a({LIN2, COL2}), .b(4'b1101), .eq(comparator_17_eq));  // open: gt, lt
  or or_22 (or_22_out, comparator_10_eq, comparator_11_eq);
  or or_23 (or_23_out, comparator_12_eq, comparator_13_eq);
  or or_24 (or_24_out, comparator_14_eq, comparator_15_eq);
  or or_25 (or_25_out, comparator_16_eq, comparator_17_eq);
  and and_111 (correct_01, or_22_out, correct);
  and and_112 (correct_11, or_23_out, correct);
  and and_113 (correct_21, or_24_out, correct);
  and and_114 (correct_31, or_25_out, correct);
  and and_115 (FIM, correct_00, correct_01, correct_02, correct_03, correct_10, correct_11, correct_12, correct_13, correct_20, correct_21, correct_22, correct_23, correct_30, correct_31, correct_32, correct_33);
  Adder #(.width(4)) adder_1 (.a(PONTOS_P1), .b(PONTOS_P2), .out(adder_1_out));  // open: cin, cout
  Comparator #(.width(4)) comparator_18 (.a({LIN1, COL1}), .b(4'b0010), .eq(comparator_18_eq));  // open: gt, lt
  or or_26 (or_26_out, comparator_18_eq, comparator_19_eq);
  Comparator #(.width(4)) comparator_19 (.a({LIN2, COL2}), .b(4'b0010), .eq(comparator_19_eq));  // open: gt, lt
  Comparator #(.width(4)) comparator_20 (.a({LIN1, COL1}), .b(4'b0110), .eq(comparator_20_eq));  // open: gt, lt
  or or_27 (or_27_out, comparator_20_eq, comparator_21_eq);
  Comparator #(.width(4)) comparator_21 (.a({LIN2, COL2}), .b(4'b0110), .eq(comparator_21_eq));  // open: gt, lt
  Comparator #(.width(4)) comparator_22 (.a({LIN1, COL1}), .b(4'b1010), .eq(comparator_22_eq));  // open: gt, lt
  or or_28 (or_28_out, comparator_22_eq, comparator_23_eq);
  Comparator #(.width(4)) comparator_23 (.a({LIN2, COL2}), .b(4'b1010), .eq(comparator_23_eq));  // open: gt, lt
  Comparator #(.width(4)) comparator_24 (.a({LIN1, COL1}), .b(4'b1110), .eq(comparator_24_eq));  // open: gt, lt
  or or_29 (or_29_out, comparator_24_eq, comparator_25_eq);
  Comparator #(.width(4)) comparator_25 (.a({LIN2, COL2}), .b(4'b1110), .eq(comparator_25_eq));  // open: gt, lt
  and and_116 (correct_02, or_26_out, correct);
  and and_117 (correct_12, or_27_out, correct);
  and and_118 (correct_22, or_28_out, correct);
  and and_119 (correct_32, or_29_out, correct);
  Comparator #(.width(4)) comparator_26 (
    .a(PONTOS_P1), .b(PONTOS_P2), .gt(comparator_26_gt), .eq(comparator_26_eq), .lt(comparator_26_lt));
  Comparator #(.width(4)) comparator_27 (.a(adder_1_out), .b(4'b1000), .eq(comparator_27_eq));  // open: gt, lt
  and and_120 (winP1, comparator_26_gt, comparator_27_eq);
  and and_121 (winP0, comparator_26_eq, comparator_27_eq);
  and and_122 (winP2, comparator_26_lt, comparator_27_eq);
  Comparator #(.width(4)) comparator_28 (.a({LIN1, COL1}), .b(4'b0011), .eq(comparator_28_eq));  // open: gt, lt
  Comparator #(.width(4)) comparator_29 (.a({LIN2, COL2}), .b(4'b0011), .eq(comparator_29_eq));  // open: gt, lt
  Comparator #(.width(4)) comparator_30 (.a({LIN1, COL1}), .b(4'b0111), .eq(comparator_30_eq));  // open: gt, lt
  Comparator #(.width(4)) comparator_31 (.a({LIN2, COL2}), .b(4'b0111), .eq(comparator_31_eq));  // open: gt, lt
  Comparator #(.width(4)) comparator_32 (.a({LIN1, COL1}), .b(4'b1011), .eq(comparator_32_eq));  // open: gt, lt
  Comparator #(.width(4)) comparator_33 (.a({LIN2, COL2}), .b(4'b1011), .eq(comparator_33_eq));  // open: gt, lt
  Comparator #(.width(4)) comparator_34 (.a({LIN1, COL1}), .b(4'b1111), .eq(comparator_34_eq));  // open: gt, lt
  Comparator #(.width(4)) comparator_35 (.a({LIN2, COL2}), .b(4'b1111), .eq(comparator_35_eq));  // open: gt, lt
  or or_30 (or_30_out, comparator_28_eq, comparator_29_eq);
  or or_31 (or_31_out, comparator_30_eq, comparator_31_eq);
  or or_32 (or_32_out, comparator_32_eq, comparator_33_eq);
  or or_33 (or_33_out, comparator_34_eq, comparator_35_eq);
  and and_123 (correct_03, or_30_out, correct);
  and and_124 (correct_13, or_31_out, correct);
  and and_125 (correct_23, or_32_out, correct);
  and and_126 (correct_33, or_33_out, correct);

  // Other names for the same wires on the sheet: savedXY1[3:0] = {LIN1, COL1}; savedXY2[3:0] = {LIN2, COL2};
  //   xy[3:0] = {LIN, COL}

  // Notes on the sheet:
  //   Conjunto de MUX que mostram ou ocultam os valores
  //   Ciência da Computação - 2024.1
  //   Prof. Ramon Nepomuceno
  //   Sebastião Sousa Soares
  //   Bruno da Silva Macedo
  //   JOGO DA MEMÓRIA
  //   Registrador das posições selecionadas
  //   Conjunto de verificadores do estado de exibição dos valores
  //   Circuitos Digitais - Computação 2024.1
  //   Gerenciador de estados
  //   Estrutura de registro e captação das coordenadas
  //   DMX responsável por indicar o LED a ser aceso
  //   Estrutura que gera o pulso de possível acerto
  //   MUX's que verifica o valor contido na "peça" escolhida por último
  //   Registra a vez do P2
  //   Registra os pontos de P1 e P2
  //   Trata erro de seleção de peça já aberta
  //   Registra a vez do P1
  //   Mostra o vencedor
  //   Conjunto de estruturas que enviam para o registrador correspondente que a peça foi "acertada"
endmodule

module geradorPseudoAleatorio (
  input  START,
  output [3:0] out_2,
  output [3:0] out_3,
  output [3:0] out_4,
  output [3:0] out_5,
  output [3:0] out_6,
  output [3:0] out_7,
  output [3:0] out_8,
  output [3:0] out_9,
  output [3:0] out_10,
  output [3:0] out_11,
  output [3:0] out_12,
  output [3:0] out_13,
  output [3:0] out_14,
  output [3:0] out_15,
  output [3:0] out_16,
  output [3:0] out_17
);

  wire v00, v01, v02, v03, v10, v11, v12, v13, v20, v21, v22, v23, v30, v31, v32, v33;
  wire [3:0] _01, _02, _03, _10, _11, _12, _13, _20, _21, _22, _23, _30, _31, _32, _33, MUX, valor;

  Counter #(.width(4), .max('hf), .ongoal("stay")) counter_1 (
    .Q(valor), .clk(START));  // open: load, D, count, carry, clr
  Random #(.width(4)) random_1 (.clk(START), .out(MUX));  // open: next, clr
  Demultiplexer #(.select(4), .enable("false")) demultiplexer_1 (
    .out0(v00), .out1(v01), .out2(v02), .out3(v03), .out4(v10), .out5(v11), .out6(v12), .out7(v13),
    .out8(v20), .out9(v21), .out10(v22), .out11(v23), .out12(v30), .out13(v31), .out14(v32), .out15(v33),
    .in(1'b1), .sel(MUX));
  Multiplexer #(.width(4), .enable("false")) multiplexer_1 (.in1(valor), .out(out_2), .sel(v00));  // open: in0
  Multiplexer #(.width(4), .enable("false")) multiplexer_2 (.in1(valor), .out(_10), .sel(v10));  // open: in0
  Multiplexer #(.width(4), .enable("false")) multiplexer_3 (.in1(valor), .out(_20), .sel(v20));  // open: in0
  Multiplexer #(.width(4), .enable("false")) multiplexer_4 (.in1(valor), .out(_30), .sel(v30));  // open: in0
  Multiplexer #(.width(4), .enable("false")) multiplexer_5 (.in1(valor), .out(_01), .sel(v01));  // open: in0
  Multiplexer #(.width(4), .enable("false")) multiplexer_6 (.in1(valor), .out(_11), .sel(v11));  // open: in0
  Multiplexer #(.width(4), .enable("false")) multiplexer_7 (.in1(valor), .out(_21), .sel(v21));  // open: in0
  Multiplexer #(.width(4), .enable("false")) multiplexer_8 (.in1(valor), .out(_31), .sel(v31));  // open: in0
  Multiplexer #(.width(4), .enable("false")) multiplexer_9 (.in1(valor), .out(_02), .sel(v02));  // open: in0
  Multiplexer #(.width(4), .enable("false")) multiplexer_10 (.in1(valor), .out(_12), .sel(v12));  // open: in0
  Multiplexer #(.width(4), .enable("false")) multiplexer_11 (.in1(valor), .out(_22), .sel(v22));  // open: in0
  Multiplexer #(.width(4), .enable("false")) multiplexer_12 (.in1(valor), .out(_32), .sel(v32));  // open: in0
  Multiplexer #(.width(4), .enable("false")) multiplexer_13 (.in1(valor), .out(_03), .sel(v03));  // open: in0
  Multiplexer #(.width(4), .enable("false")) multiplexer_14 (.in1(valor), .out(_13), .sel(v13));  // open: in0
  Multiplexer #(.width(4), .enable("false")) multiplexer_15 (.in1(valor), .out(_23), .sel(v23));  // open: in0
  Multiplexer #(.width(4), .enable("false")) multiplexer_16 (.in1(valor), .out(_33), .sel(v33));  // open: in0

  // Other names for the same wires on the sheet: _00[3:0] = out_2
endmodule
